// Logisim project parte1_cache.circ as structural Verilog: 3 circuits, main circuit main
module main (
  input  RESET_CONT,
  input  [5:0] ENDERECO,
  input  RESET,
  output OFFSET,
  output out_5
);

  wire CLK_out, d_ff_1_q, d_ff_2_q, d_ff_3_q, d_ff_4_q, decoder_1_out0, decoder_1_out1, decoder_1_out2,
       decoder_1_out3, multiplexer_1_out, multiplexer_2_out, multiplexer_3_out, multiplexer_4_out,
       multiplexer_5_out, not_1_out, not_2_out, or_1_out, xor_sintetizado_1_s, xor_sintetizado_2_s,
       xor_sintetizado_3_s;
  wire [2:0] MEMORIA_TAG_dout;
  wire [3:0] counter_1_q;

  Clock CLK (.out(CLK_out));
  Multiplexer multiplexer_1 (.in0(d_ff_1_q), .in1(1'b1), .out(multiplexer_1_out), .sel(decoder_1_out0));
  Multiplexer multiplexer_2 (.in0(d_ff_2_q), .in1(1'b1), .out(multiplexer_2_out), .sel(decoder_1_out1));
  Multiplexer multiplexer_3 (.in0(d_ff_3_q), .in1(1'b1), .out(multiplexer_3_out), .sel(decoder_1_out2));
  Multiplexer multiplexer_4 (.in0(d_ff_4_q), .in1(1'b1), .out(multiplexer_4_out), .sel(decoder_1_out3));
  D_Flip_Flop d_ff_1 (.D(multiplexer_1_out), .clk(CLK_out), .Q(d_ff_1_q), .reset(RESET));  // open: Qn, preset
  D_Flip_Flop d_ff_2 (.D(multiplexer_2_out), .clk(CLK_out), .Q(d_ff_2_q), .reset(RESET));  // open: Qn, preset
  D_Flip_Flop d_ff_3 (.D(multiplexer_3_out), .clk(CLK_out), .Q(d_ff_3_q), .reset(RESET));  // open: Qn, preset
  D_Flip_Flop d_ff_4 (.D(multiplexer_4_out), .clk(CLK_out), .Q(d_ff_4_q), .reset(RESET));  // open: Qn, preset
  RAM #(.addrWidth(2), .dataWidth(3)) MEMORIA_TAG (
    .addr(ENDERECO[2:1]), .we(not_1_out), .oe(1'b1), .clk(CLK_out), .din(ENDERECO[5:3]),
    .dout(MEMORIA_TAG_dout));
  not not_1 (not_1_out, out_5);
  Multiplexer #(.select(2)) multiplexer_5 (
    .in0(d_ff_1_q), .in1(d_ff_2_q), .in2(d_ff_3_q), .in3(d_ff_4_q), .out(multiplexer_5_out),
    .sel(ENDERECO[2:1]));
  LED OFFSET_LED (.in(ENDERECO[0]));
  Decoder #(.enable("false"), .select(2)) decoder_1 (
    .out0(decoder_1_out0), .out1(decoder_1_out1), .out2(decoder_1_out2), .out3(decoder_1_out3),
    .sel(ENDERECO[2:1]));
  xor_sintetizado xor_sintetizado_1 (.A(ENDERECO[3]), .B(MEMORIA_TAG_dout[0]), .S(xor_sintetizado_1_s));
  xor_sintetizado xor_sintetizado_2 (.A(ENDERECO[4]), .B(MEMORIA_TAG_dout[1]), .S(xor_sintetizado_2_s));
  xor_sintetizado xor_sintetizado_3 (.A(ENDERECO[5]), .B(MEMORIA_TAG_dout[2]), .S(xor_sintetizado_3_s));
  or or_1 (or_1_out, xor_sintetizado_1_s, xor_sintetizado_2_s, xor_sintetizado_3_s);
  LED led_1 (.in(out_5));
  not not_2 (not_2_out, or_1_out);
  and and_1 (out_5, not_2_out, multiplexer_5_out);
  Counter #(.max('hf), .width(4)) counter_1 (
    .clr(RESET_CONT), .clk(out_5), .Q(counter_1_q));  // open: load, up, count, D, carry
  // BCD_to_7_Segment_decoder bcd_to_7_segment_decoder_1: pin names not known; wires that end beside it: counter_1_q
  _7_Segment_Display u_7_segment_display_1 ();  // open: g, f, a, b, e, d, c, dp

  assign OFFSET = ENDERECO[0];

  // Notes on the sheet:
  //   CONSTANTE 1
  //   BIT DE VALIDAÇÃO DE 4 LINHAS
  //   DESLOCAMENTO A0
  //   INDEX A2-A1
  //   TAG A5-A3
  //   BIT DE VALIDADE
  //   T0-T1-T2
  //   S0-S1-S2
  //   PORTA XOR SINTETIZADAS T0,T1,T2 - S0,S1,S2
  //   VALIDO
  //   ACERTO
endmodule

module flip_flops_vs1 (
  input  in_1,
  input  in_2
);

  wire d_ff_1_q, d_ff_2_q, d_ff_3_q, d_ff_4_q;

  D_Flip_Flop d_ff_1 (.D(1'b1), .clk(in_2), .Q(d_ff_1_q), .reset(in_1));  // open: Qn, preset
  D_Flip_Flop d_ff_2 (.D(1'b1), .clk(in_2), .Q(d_ff_2_q), .reset(in_1));  // open: Qn, preset
  D_Flip_Flop d_ff_3 (.D(1'b1), .clk(in_2), .Q(d_ff_3_q), .reset(in_1));  // open: Qn, preset
  D_Flip_Flop d_ff_4 (.D(1'b1), .clk(in_2), .Q(d_ff_4_q), .reset(in_1));  // open: Qn, preset
  Multiplexer #(.select(2)) multiplexer_1 (
    .in0(d_ff_1_q), .in1(d_ff_2_q), .in2(d_ff_3_q), .in3(d_ff_4_q));  // open: out, sel
endmodule

module xor_sintetizado (
  input  A,
  input  B,
  output S
);

  wire and_1_out, and_2_out, not_1_out, not_2_out;

  not not_1 (not_1_out, B);
  not not_2 (not_2_out, A);
  and and_1 (and_1_out, A, not_1_out);
  and and_2 (and_2_out, B, not_2_out);
  or or_1 (S, and_1_out, and_2_out);
endmodule
